# Fritzing sketch Arduino MIDI Sound Module (saved by Fritzing 0.9.3b)
breadboards: 1

parts:
  Part1 = Arduino Uno (Rev3) - ICSP
  OLED_SPI1 = OLED 128x64 SPI Monochrome Display
  R2 = Resistor [tolerance=±1% resistance=3.9k package=THT]
  R3 = Resistor [tolerance=±1% resistance=1M package=THT]
  R3_2 = Resistor [tolerance=±1% resistance=1M package=THT]
  R1 = Resistor [tolerance=±1% resistance=3.9k package=THT]
  C1 = Electrolytic Capacitor [capacitance=10µF voltage=50V package="100 mil [THT, electrolytic]"]
  C2 = Ceramic Capacitor [capacitance=3.3nF package="200 mil [THT, multilayer]"]
  TRS1 = Audio Jack (TRS) 3.5mm [package="4Ucon 08780 [THT]"]

nets:
  5V: Part1.5V, OLED_SPI1.VCC
  N1: Part1.ICSP_SCK, Part1.D13/SCK, OLED_SPI1.D0
  N2: Part1.ICSP_MOSI, Part1.D11_PWM/MOSI, OLED_SPI1.D1
  N3: Part1.GND, C2.1, TRS1.Sleeve
  N4: Part1.D9_PWM, R3.Pin_0
  N5: Part1.D10_PWM/SS, R1.Pin_0
  N6: Part1.D2, OLED_SPI1.RES
  N7: Part1.D3_PWM, OLED_SPI1.DC
  N8: Part1.D4, OLED_SPI1.CS
  N9: Part1.D5_PWM, R3_2.Pin_0
  N10: Part1.D6_PWM, R2.Pin_0
  N11: Part1.D7, OLED_SPI1.GND
  N12: R2.Pin_1, R3.Pin_1, R3_2.Pin_1, R1.Pin_1, C1.+, C2.0
  N13: C1.-, TRS1.Ring, TRS1.Tip
